# Fritzing sketch AQI (saved by Fritzing 0.9.3b)
breadboards: 1

parts:
  Arduino_Mega = Arduino Mega 2560 (Rev3)
  DHT22-Temperature_and_Humidity_sensor = Humidity and Temperature Sensor RHT03
  MQ5-_LPG_Flammable_gas = Gas Sensor Breakout Board
  MQ135(All) = Gas Sensor Breakout Board
  MQ7_-_CO_sensor = Gas Sensor Breakout Board
  MQ8_-_H2_sensor = Gas Sensor Breakout Board
  Flame_Sensor = KY-026 Flame Sensor Module [package="Breakout board"]
  1207_Passive_buzzer = Piezo Buzzer
  OLED_Display = Grove OLED 128x96
  Particle_sensor = SDS011 - dust sensor [part_number=1]
  ESP_8266-01_wifi_module = ESP8266 WiFi Module [part_number=ESP8266]
  2_ohm = Resistor [tolerance=±5% resistance=220 package="2512 [SMD]"]
  1_ohm = Resistor [tolerance=±5% resistance=220 package="0402 [SMD]"]
  10_ohm = Resistor [tolerance=±5% resistance=220 package="0402 [SMD]"]
  SW-1 = Vibration sensor module  # not connected

nets:
  N1: Arduino_Mega.A0, MQ135(All).AOUT
  N2: Arduino_Mega.A1, MQ7_-_CO_sensor.AOUT
  N3: Arduino_Mega.A2, MQ8_-_H2_sensor.AOUT
  N4: Arduino_Mega.A3, MQ5-_LPG_Flammable_gas.AOUT
  N5: Arduino_Mega.A4, Flame_Sensor.A0
  N6: Arduino_Mega.D21/SCL, OLED_Display.SCL
  N7: Arduino_Mega.D20/SDA, OLED_Display.SDA
  5V: Arduino_Mega.5V, DHT22-Temperature_and_Humidity_sensor.Vcc, MQ5-_LPG_Flammable_gas.5V, MQ135(All).5V, MQ7_-_CO_sensor.5V, MQ8_-_H2_sensor.5V, Flame_Sensor.+, OLED_Display.VCC, Particle_sensor.5v, ESP_8266-01_wifi_module.VCC, 10_ohm.Pin_0
  GND: Arduino_Mega.GND, DHT22-Temperature_and_Humidity_sensor.GND_1, MQ5-_LPG_Flammable_gas.GND, MQ135(All).GND, MQ7_-_CO_sensor.GND, MQ8_-_H2_sensor.GND, Flame_Sensor.G, 1207_Passive_buzzer.pin_2, OLED_Display.GND, Particle_sensor.GND, ESP_8266-01_wifi_module.GND, 2_ohm.Pin_0
  N8: Arduino_Mega.D0_RX0, Particle_sensor.RX
  N9: Arduino_Mega.D1_TX0, Particle_sensor.TX
  N10: Arduino_Mega.D2_PWM, DHT22-Temperature_and_Humidity_sensor.Data-signal
  N11: Arduino_Mega.D3_PWM, ESP_8266-01_wifi_module.TXD
  N12: Arduino_Mega.D4_PWM, 1_ohm.Pin_1
  N13: Arduino_Mega.D6_PWM, Flame_Sensor.D0
  N14: Arduino_Mega.D7_PWM, 1207_Passive_buzzer.pin_1
  N15: ESP_8266-01_wifi_module.RXD, 2_ohm.Pin_1, 1_ohm.Pin_0
  N16: ESP_8266-01_wifi_module.CH_PD, 10_ohm.Pin_1

custom parts:
  Gas Sensor Breakout Board: Gas sensor breakout board. Input voltage is 5V. Sensor output is available in analog and digital.
  KY-026 Flame Sensor Module: KY-026 Flame Sensor Module reacts in the presence of fire.
  Piezo Buzzer: Part from https://www.nutsvolts.com/magazine/article/november2012_SmileysWorkshop. Breadboard and icon images modified to be 0.3" in spacing and be more similar to the actual physical part.
  SDS011 - dust sensor: The SDS 011 Sensor is a quite recent Air Quality Sensor developed by inovafit, a spin-off from the university of Jinan (in Shandong). With its size, it is probably one of the best sensor in terms of accuracy: While other sensors tend to focus on shrinking the sensor size, the SDS 011 has opted for a size tradeoff allowing it to use a larger fan. And the larger the fan, the better the quality.
  ESP8266 WiFi Module: Generic WiFi Module based on the ESP8266 with onboard PCB antenna and UART communications
  Vibration sensor module: Single-roller type full induction trigger switch. When no vibration or tilt, the product is ON conduction state, and in the steady state, when a vibration or tilt, the switch will be rendered instantly disconnect the conductive resistance increases, generating a current pulse signal, thereby triggering circuit. The default state of the swith is close Digital output Supply voltage:3.3V-5V On-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
