# Fritzing sketch arduino_project (saved by Fritzing 0.9.3b)
breadboards: 2

parts:
  Arduino_Mega = Arduino Mega 2560 (Rev3) [part_number=2560]
  DHT22 = Humidity and Temperature Sensor RHT03
  MQ5-_LPG_Flammable_gas = Gas Sensor Breakout Board
  MQ135_(Mix_Gases) = Gas Sensor Breakout Board
  MQ7_-_CO_sensor = Gas Sensor Breakout Board
  MQ8_-_H2_sensor = Gas Sensor Breakout Board
  Flame_Sensor = KY-026 Flame Sensor Module [package="Breakout board"]
  1207_Passive_buzzer = Piezo Buzzer
  OLED_Display = Grove OLED 128x96
  Particle_sensor = SDS011 - dust sensor [part_number=1]
  C1 = Electrolytic Capacitor [capacitance=0.1mF package="100 mil [THT, electrolytic]"]
  C2 = Electrolytic Capacitor [capacitance=0.1mF package="100 mil [THT, electrolytic]"]
  C3 = Electrolytic Capacitor [capacitance=0.1mF package="100 mil [THT, electrolytic]"]
  C4 = Electrolytic Capacitor [capacitance=0.1mF package="100 mil [THT, electrolytic]"]
  C5 = Tantalum Capacitor [capacitance=10nF package="D 7343 [SMD, tantalum]"]
  C6 = Tantalum Capacitor [capacitance=10nF package="D 7343 [SMD, tantalum]"]
  C7 = Tantalum Capacitor [capacitance=10nF package="D 7343 [SMD, tantalum]"]
  C8 = Tantalum Capacitor [capacitance=10nF package="D 7343 [SMD, tantalum]"]
  U1 = ESP8266 WiFi Module [part_number="ESP8266-01 Wifi Module"]
  R1 = Resistor [tolerance=±5% resistance=1k package="1206 [SMD]"]
  R2 = Resistor [tolerance=±5% resistance=2.2k package="0402 [SMD]"]
  R3 = Resistor [tolerance=±5% resistance=10k package="0805 [SMD]"]
  S4 = Pushbutton [part_number=Reset package="[SMD]"]
  S5 = Pushbutton [part_number="Control Buttons" package="[SMD]"]
  S6 = Pushbutton [package="[SMD]"]
  S7 = Pushbutton [package="[SMD]"]
  R4 = Resistor [tolerance=±5% resistance=100k package="0603 [SMD]"]
  R5 = Resistor [tolerance=±5% resistance=100k package="0603 [SMD]"]
  R6 = Resistor [tolerance=±5% resistance=100k package="0603 [SMD]"]
  R7 = Resistor [tolerance=±5% resistance=100k package="0603 [SMD]"]
  LED3 = LED - 5mm [color="Green (555nm)" part_number=power package="5 mm [THT]"]
  LED4 = RGB LED (com. cathode, rgb) [part_number=Alarm package="5 mm [THT]"]
  LED5 = LED - 5mm [color="Blue (430nm)" part_number="Server Connection" package="5 mm [THT]"]
  LED6 = LED - 5mm [color="Red (633nm)" part_number="System Error" package="5 mm [THT]"]
  LED7 = LED - 5mm [color="Yellow (592nm)" part_number="Processing User Input" package="5 mm [THT]"]
  R8 = Resistor [tolerance=±5% resistance=220 package="0603 [SMD]"]
  R9 = Resistor [tolerance=±5% resistance=220 package="0603 [SMD]"]
  R10 = Resistor [tolerance=±5% resistance=220 package="0603 [SMD]"]
  R11 = Resistor [tolerance=±5% resistance=220 package="0603 [SMD]"]
  R12 = Resistor [tolerance=±5% resistance=220 package="0603 [SMD]"]
  R14 = Resistor [tolerance=±5% resistance=220 package="0603 [SMD]"]
  R15 = Resistor [tolerance=±5% resistance=220 package="0603 [SMD]"]
  S8 = Pushbutton [package="[SMD]"]
  R16 = Resistor [tolerance=±5% resistance=100k package="0603 [SMD]"]

nets:
  N1: Arduino_Mega.A0, MQ135_(Mix_Gases).AOUT, C8.+
  N2: Arduino_Mega.A1, MQ7_-_CO_sensor.AOUT, C7.+
  N3: Arduino_Mega.A2, MQ8_-_H2_sensor.AOUT, C6.+
  N4: Arduino_Mega.A3, MQ5-_LPG_Flammable_gas.AOUT, C5.+
  N5: Arduino_Mega.A4, Flame_Sensor.A0
  N6: Arduino_Mega.D21/SCL, OLED_Display.SCL
  N7: Arduino_Mega.D20/SDA, OLED_Display.SDA
  N8: Arduino_Mega.D19/RX1, U1.RST, U1.TXD
  N9: Arduino_Mega.D18/TX1, R1.Pin_1
  GND: Arduino_Mega.GND, DHT22.GND_1, MQ5-_LPG_Flammable_gas.GND, MQ135_(Mix_Gases).GND, MQ7_-_CO_sensor.GND, MQ8_-_H2_sensor.GND, Flame_Sensor.G, 1207_Passive_buzzer.pin_2, OLED_Display.GND, Particle_sensor.GND, C1.-, C2.-, C3.-, C4.-, C5.-, C6.-, C7.-, C8.-, U1.GPIO_0, U1.GND, R2.Pin_1, S4.Pin_3, S4.Pin_4, S5.Pin_3, S5.Pin_4, S6.Pin_3, S6.Pin_4, S7.Pin_3, S7.Pin_4, LED3.cathode, LED4.common_cathode, LED5.cathode, LED6.cathode, LED7.cathode, S8.Pin_3, S8.Pin_4
  N10: Arduino_Mega.D11_PWM, S8.Pin_1, S8.Pin_2, R16.Pin_1
  N11: Arduino_Mega.D10_PWM, S5.Pin_1, S5.Pin_2, R5.Pin_1
  N12: Arduino_Mega.D9_PWM, S6.Pin_1, S6.Pin_2, R6.Pin_1
  N13: Arduino_Mega.D8_PWM, S7.Pin_1, S7.Pin_2, R7.Pin_1
  N14: Arduino_Mega.RESET, S4.Pin_1, S4.Pin_2, R4.Pin_1
  3V3: Arduino_Mega.3V3, U1.VCC
  5V: Arduino_Mega.5V, DHT22.Vcc, MQ5-_LPG_Flammable_gas.5V, MQ135_(Mix_Gases).5V, MQ7_-_CO_sensor.5V, MQ8_-_H2_sensor.5V, Flame_Sensor.+, OLED_Display.VCC, Particle_sensor.5v, C1.+, C2.+, C3.+, C4.+, R3.Pin_1, R4.Pin_0, R5.Pin_0, R6.Pin_0, R7.Pin_0, R16.Pin_0
  N15: Arduino_Mega.D2_PWM, DHT22.Data-signal
  N16: Arduino_Mega.D3_PWM, Particle_sensor.1_un
  N17: Arduino_Mega.D4_PWM, Particle_sensor.25_un
  N18: Arduino_Mega.D5_PWM, 1207_Passive_buzzer.pin_1
  N19: Arduino_Mega.D31, R8.Pin_0
  N20: Arduino_Mega.D33, R9.Pin_0
  N21: Arduino_Mega.D35, R10.Pin_0
  N22: Arduino_Mega.D37, R12.Pin_0
  N23: Arduino_Mega.D45, R14.Pin_0
  N24: Arduino_Mega.D47, R15.Pin_0
  N25: Arduino_Mega.D49, R11.Pin_0
  N26: U1.RXD, R1.Pin_0, R2.Pin_0
  N27: U1.CH_PD, R3.Pin_0
  N28: LED3.anode, R8.Pin_1
  N29: LED4.red_anode, R14.Pin_1
  N30: LED4.green_anode, R15.Pin_1
  N31: LED4.blue_anode, R11.Pin_1
  N32: LED5.anode, R9.Pin_1
  N33: LED6.anode, R12.Pin_1
  N34: LED7.anode, R10.Pin_1

notes:
  Industrial Env ironment Quality Monitoring & Hazard Detection System
  Project Members
  --------------------------
  Muhammed Humam Hossain 202111078
  Mahmudur Rahman Marfy 202111072
  Saihan Bin Sajjad 202111075
  Md Mahmudur Rahman 202111020

custom parts:
  Gas Sensor Breakout Board: Gas sensor breakout board. Input voltage is 5V. Sensor output is available in analog and digital.
  KY-026 Flame Sensor Module: KY-026 Flame Sensor Module reacts in the presence of fire.
  Piezo Buzzer: Part from https://www.nutsvolts.com/magazine/article/november2012_SmileysWorkshop. Breadboard and icon images modified to be 0.3" in spacing and be more similar to the actual physical part.
  SDS011 - dust sensor: The SDS 011 Sensor is a quite recent Air Quality Sensor developed by inovafit, a spin-off from the university of Jinan (in Shandong). With its size, it is probably one of the best sensor in terms of accuracy: While other sensors tend to focus on shrinking the sensor size, the SDS 011 has opted for a size tradeoff allowing it to use a larger fan. And the larger the fan, the better the quality.
  ESP8266 WiFi Module: Generic WiFi Module based on the ESP8266 with onboard PCB antenna and UART communications
